// Logisim project circutioquedecidea.circ as structural Verilog: 4 circuits, main circuit main
module main (
  input  in_1,
  input  [8:0] in_2
);

  wire bcd_to_7_segment_decoder_1_p1, binary_to_bcd_converter_1_p3, binary_to_bcd_converter_1_p4, clock_1_out;
  wire [8:0] counter_1_q, rom_1_data;

  Clock clock_1 (.out(clock_1_out));
  Counter #(.max('h1ff), .width(9)) counter_1 (
    .load(in_1), .clk(clock_1_out), .D(rom_1_data), .Q(counter_1_q));  // open: clr, up, count, carry
  _7_Segment_Display u_7_segment_display_1 ();  // open: g, f, a, b, e, d, c, dp
  // BCD_to_7_Segment_decoder bcd_to_7_segment_decoder_1: pin names not known; wires that end beside it: bcd_to_7_segment_decoder_1_p1
  // Binary_to_BCD_converter binary_to_bcd_converter_1: pin names not known; wires that end beside it: counter_1_q, bcd_to_7_segment_decoder_1_p1, binary_to_bcd_converter_1_p3, binary_to_bcd_converter_1_p4
  ROM #(.addrWidth(9), .dataWidth(9)) rom_1 (.addr(counter_1_q), .data(rom_1_data));
  _7_Segment_Display u_7_segment_display_2 ();  // open: g, f, a, b, e, d, c, dp
  _7_Segment_Display u_7_segment_display_3 ();  // open: g, f, a, b, e, d, c, dp
  // BCD_to_7_Segment_decoder bcd_to_7_segment_decoder_2: pin names not known; wires that end beside it: binary_to_bcd_converter_1_p3
  // BCD_to_7_Segment_decoder bcd_to_7_segment_decoder_3: pin names not known; wires that end beside it: binary_to_bcd_converter_1_p4

  // Notes on the sheet:
  //   contents of rom_1 (hex, n*v repeats v):
  //   7c 4*0 174 56*0 5 32*0 3e 28*0 5f 247*0 1db 102*0 1f
endmodule

module a (
  input  INPUTT,
  input  F123,
  input  F4in,
  output Aoutput
);

  wire and_1_out, and_2_out, F1F2F3_out, F4_out, not_1_out, not_2_out, not_3_out;

  or or_1 (Aoutput, F1F2F3_out, 1'b0, F4_out);
  or F4 (F4_out, and_1_out, and_2_out);
  or F1F2F3 (F1F2F3_out, F123, INPUTT);
  and and_1 (and_1_out, INPUTT, F4in);
  and and_2 (and_2_out, not_3_out, not_1_out);
  not not_1 (not_1_out, INPUTT);
  not not_2 (not_2_out, F123);
  not not_3 (not_3_out, F4in);

  // Notes on the sheet:
  //   F5
endmodule

module i0o124 (
  input  [8:0] INPU,
  output OUTPU
);

  // AND_Gate and_1 has open pins: in0=INPU[0], in1=INPU[1], in2=INPU[2], in3=INPU[3], in4=INPU[4], in5=INPU[5], in6=INPU[6], in7=INPU[7], in8=INPU[8], out=open
endmodule

module decideSalida9bits (
  input  [8:0] Entrada,
  input  F1,
  input  F2,
  input  F3,
  input  F4,
  input  F5,
  output E475
);

  wire E0_out, E5_out, E31_out, E62_out, E95_out, E124_out, E372_out, not_1_out, not_2_out, not_3_out,
       not_4_out, not_5_out, not_6_out, not_7_out, not_8_out, not_9_out, not_10_out, not_11_out, not_12_out,
       not_13_out, not_14_out;

  not not_1 (not_1_out, F1);
  not not_2 (not_2_out, F2);
  not not_3 (not_3_out, F3);
  not not_4 (not_4_out, F4);
  not not_5 (not_5_out, F5);
  not not_6 (not_6_out, Entrada[0]);
  not not_7 (not_7_out, Entrada[5]);
  and E0 (E0_out, not_6_out, not_7_out, not_8_out);
  LED led_1 (.in(E0_out));
  not not_8 (not_8_out, Entrada[8]);
  not not_9 (not_9_out, Entrada[8]);
  and E124 (E124_out, not_9_out, Entrada[5], not_10_out);
  not not_10 (not_10_out, Entrada[1]);
  and E95 (E95_out, Entrada[6], Entrada[1], Entrada[2]);
  LED led_2 (.in(E95_out));
  and E62 (E62_out, Entrada[5], not_11_out);
  LED led_3 (.in(E62_out));
  not not_11 (not_11_out, Entrada[6]);
  not not_12 (not_12_out, Entrada[1]);
  and E5 (E5_out, not_12_out, Entrada[0]);
  LED led_4 (.in(E5_out));
  and E372 (E372_out, Entrada[8], not_13_out);
  LED led_5 (.in(E372_out));
  not not_13 (not_13_out, Entrada[7]);
  LED led_6 (.in(Entrada[7]));
  not not_14 (not_14_out, Entrada[6]);
  and E31 (E31_out, not_14_out, Entrada[1], Entrada[0]);
  LED led_7 (.in(E31_out));
  LED led_8 (.in(E124_out));
  // AND_Gate E124A has open pins: in0=E124_out, in1=F1, out=open

  assign E475 = Entrada[7];
endmodule
